// Logisim project USR.circ as structural Verilog: 1 circuit, main circuit main
module main (
);

  wire clock_1_out, d_ff_1_q, d_ff_2_q, d_ff_3_q, d_ff_4_q, dipswitch_2_sw1, dipswitch_2_sw2,
       dipswitch_2_sw3, dipswitch_2_sw4, multiplexer_1_out, multiplexer_2_out, multiplexer_3_out,
       multiplexer_4_out;
  wire [1:0] dipswitch_1_sw2;

  DipSwitch #(.number(2)) dipswitch_1 (.sw1(dipswitch_1_sw2[1]), .sw2(dipswitch_1_sw2[0]));
  DipSwitch #(.number(4)) dipswitch_2 (
    .sw1(dipswitch_2_sw1), .sw2(dipswitch_2_sw2), .sw3(dipswitch_2_sw3), .sw4(dipswitch_2_sw4));
  Clock clock_1 (.out(clock_1_out));
  Multiplexer #(.select(2), .enable("false")) multiplexer_1 (
    .in0(d_ff_1_q), .in1(d_ff_2_q), .in2(d_ff_4_q), .in3(dipswitch_2_sw4), .out(multiplexer_1_out),
    .sel(dipswitch_1_sw2));
  D_Flip_Flop d_ff_1 (.D(multiplexer_1_out), .clk(clock_1_out), .Q(d_ff_1_q));  // open: Qn, preset, reset
  Multiplexer #(.select(2), .enable("false")) multiplexer_2 (
    .in0(d_ff_2_q), .in1(d_ff_3_q), .in2(d_ff_1_q), .in3(dipswitch_2_sw3), .out(multiplexer_2_out),
    .sel(dipswitch_1_sw2));
  D_Flip_Flop d_ff_2 (.D(multiplexer_2_out), .clk(clock_1_out), .Q(d_ff_2_q));  // open: Qn, preset, reset
  Multiplexer #(.select(2), .enable("false")) multiplexer_3 (
    .in0(d_ff_3_q), .in1(d_ff_4_q), .in2(d_ff_2_q), .in3(dipswitch_2_sw2), .out(multiplexer_3_out),
    .sel(dipswitch_1_sw2));
  D_Flip_Flop d_ff_3 (.D(multiplexer_3_out), .clk(clock_1_out), .Q(d_ff_3_q));  // open: Qn, preset, reset
  Multiplexer #(.select(2), .enable("false")) multiplexer_4 (
    .in0(d_ff_4_q), .in1(d_ff_1_q), .in2(d_ff_3_q), .in3(dipswitch_2_sw1), .out(multiplexer_4_out),
    .sel(dipswitch_1_sw2));
  D_Flip_Flop d_ff_4 (.D(multiplexer_4_out), .clk(clock_1_out), .Q(d_ff_4_q));  // open: Qn, preset, reset
  LED led_1 (.in(d_ff_4_q));
endmodule
