// Logisim project shift_registers.circ as structural Verilog: 1 circuit, main circuit main
module main (
);

  wire and_1_out, and_2_out, and_3_out, and_4_out, and_5_out, and_6_out, clock_1_out, d_ff_1_q, d_ff_2_q,
       d_ff_3_q, d_ff_4_q, d_ff_5_q, d_ff_6_q, d_ff_7_q, d_ff_8_q, dipswitch_1_sw1, dipswitch_1_sw2,
       dipswitch_1_sw3, dipswitch_1_sw4, dipswitch_2_sw1, dipswitch_2_sw4, dipswitch_2_sw8, not_1_out,
       or_1_out, or_2_out, or_3_out, undriven;

  DipSwitch dipswitch_1 (
    .sw1(dipswitch_1_sw1), .sw2(dipswitch_1_sw2), .sw3(dipswitch_1_sw3), .sw4(dipswitch_1_sw4));  // open: sw5, sw6, sw7, sw8
  DipSwitch dipswitch_2 (
    .sw1(dipswitch_2_sw1), .sw4(dipswitch_2_sw4), .sw8(dipswitch_2_sw8));  // open: sw2, sw3, sw5, sw6, sw7
  Clock clock_1 (.out(clock_1_out));
  Clock clock_2 ();  // open: out
  not not_1 (not_1_out, dipswitch_2_sw1);
  and and_1 (and_1_out, d_ff_1_q, not_1_out);
  or or_1 (or_1_out, and_1_out, and_2_out);
  D_Flip_Flop d_ff_1 (.D(dipswitch_1_sw1), .clk(clock_1_out), .Q(d_ff_1_q));  // open: Qn, preset, reset
  D_Flip_Flop d_ff_2 (.D(dipswitch_2_sw8), .clk(undriven), .Q(d_ff_2_q), .reset(dipswitch_2_sw1));  // open: Qn, preset
  and and_2 (and_2_out, dipswitch_2_sw1, dipswitch_1_sw2);
  LED led_1 (.in(d_ff_2_q));
  D_Flip_Flop d_ff_3 (.D(d_ff_2_q), .clk(undriven), .Q(d_ff_3_q), .reset(dipswitch_2_sw1));  // open: Qn, preset
  and and_3 (and_3_out, d_ff_4_q, not_1_out);
  or or_2 (or_2_out, and_3_out, and_4_out);
  D_Flip_Flop d_ff_4 (.D(or_1_out), .clk(clock_1_out), .Q(d_ff_4_q));  // open: Qn, preset, reset
  LED led_2 (.in(d_ff_3_q));
  D_Flip_Flop d_ff_5 (.D(d_ff_3_q), .clk(undriven), .Q(d_ff_5_q), .reset(dipswitch_2_sw1));  // open: Qn, preset
  and and_4 (and_4_out, dipswitch_2_sw1, dipswitch_1_sw3);
  LED led_3 (.in(d_ff_5_q));
  D_Flip_Flop d_ff_6 (.D(d_ff_5_q), .clk(undriven), .Q(d_ff_6_q), .reset(dipswitch_2_sw1));  // open: Qn, preset
  and and_5 (and_5_out, d_ff_7_q, not_1_out);
  D_Flip_Flop d_ff_7 (.D(or_2_out), .clk(clock_1_out), .Q(d_ff_7_q));  // open: Qn, preset, reset
  LED led_4 (.in(d_ff_6_q));
  and and_6 (and_6_out, dipswitch_2_sw1, dipswitch_1_sw4);
  or or_3 (or_3_out, and_5_out, and_6_out);
  D_Flip_Flop d_ff_8 (.D(or_3_out), .clk(clock_1_out), .Q(d_ff_8_q));  // open: Qn, preset, reset
  LED led_5 (.in(d_ff_8_q));
endmodule
